// Logisim project p3.circ as structural Verilog: 1 circuit, main circuit main
module main (
  input  in_1,
  output out_2
);

  wire clock_1_out, d_ff_1_q, d_ff_2_q, d_ff_3_q, multiplexer_1_out, not_1_out, not_2_out, xor_1_out;

  not not_1 (not_1_out, in_1);
  Clock clock_1 (.out(clock_1_out));
  Multiplexer multiplexer_1 (.in0(not_1_out), .in1(d_ff_3_q), .out(multiplexer_1_out), .sel(d_ff_1_q));
  D_Flip_Flop d_ff_1 (.D(1'b1), .clk(clock_1_out), .Q(d_ff_1_q));  // open: Qn, preset, reset
  D_Flip_Flop d_ff_2 (.D(multiplexer_1_out), .clk(clock_1_out), .Q(d_ff_2_q));  // open: Qn, preset, reset
  D_Flip_Flop d_ff_3 (.D(in_1), .clk(clock_1_out), .Q(d_ff_3_q));  // open: Qn, preset, reset
  xor xor_1 (xor_1_out, d_ff_2_q, d_ff_3_q);
  not not_2 (not_2_out, xor_1_out);
  and and_1 (out_2, d_ff_1_q, not_2_out);
endmodule
