// Logisim project ex5.circ as structural Verilog: 1 circuit, main circuit Running_LED
module Running_LED (
  input  [7:0] INITIAL_LED,
  input  RST,
  output [7:0] OUT_LED
);

  wire clock_1_out, comparator_1_lt;
  wire [3:0] CNT;
  wire [7:0] multiplexer_1_out, register_1_q;

  Clock clock_1 (.out(clock_1_out));
  LED led_1 (.in(OUT_LED[7]));
  Multiplexer #(.width(8)) multiplexer_1 (.in0(register_1_q), .in1(INITIAL_LED), .out(multiplexer_1_out), .sel(RST));
  LED led_2 (.in(OUT_LED[6]));
  LED led_3 (.in(OUT_LED[5]));
  Register register_1 (
    .D(multiplexer_1_out), .clk(clock_1_out), .Q({register_1_q[6:0], register_1_q[7]}));  // open: en, clr
  LED led_4 (.in(OUT_LED[4]));
  Multiplexer #(.width(8)) multiplexer_2 (.in0(OUT_LED), .in1(register_1_q), .out(OUT_LED), .sel(comparator_1_lt));
  LED led_5 (.in(OUT_LED[3]));
  LED led_6 (.in(OUT_LED[2]));
  Comparator #(.mode("unsigned"), .width(4)) comparator_1 (.a(CNT), .b(4'b1000), .lt(comparator_1_lt));  // open: gt, eq
  LED led_7 (.in(OUT_LED[1]));
  LED led_8 (.in(OUT_LED[0]));
  Counter #(.max('hf), .width(4)) counter_1 (
    .clr(RST), .up(1'b1), .clk(clock_1_out), .Q(CNT));  // open: load, count, D, carry

  // Notes on the sheet:
  //   PUT CIRCUITS HERE
endmodule
