// Logisim project ex2.circ as structural Verilog: 1 circuit, main circuit main
module main (
  input  clk,
  input  rst,
  input  pc_update,
  input  [31:0] new_addr,
  output [31:0] current_addr
);

  wire [31:0] adder_1_out, aligned_addr, multiplexer_1_out;

  assign aligned_addr = new_addr & 32'hfffffffc;  // AND_Gate and_1, 32 bits wide
  Adder #(.width(32)) adder_1 (.a(current_addr), .b(32'h4), .out(adder_1_out));  // open: cin, cout
  Multiplexer #(.width(32)) multiplexer_1 (
    .in0(adder_1_out), .in1(aligned_addr), .out(multiplexer_1_out), .sel(pc_update));
  Register #(.width(32)) register_1 (.D(multiplexer_1_out), .clk(clk), .Q(current_addr), .clr(rst));  // open: en
endmodule
